# Fritzing sketch ultraschall_abstandsmesser (saved by Fritzing 1.0.5)
circuit board: 15.1212cm x 5.68577cm
breadboards: 1

parts:
  R1 = Resistor [tolerance=±5% power=0.25W resistance=2.2k package=THT]
  R2 = Resistor [tolerance=±5% power=0.25W resistance=2.2k package=THT]
  R3 = Resistor [tolerance=±5% power=0.25W resistance=2.2k package=THT]
  R4 = Resistor [tolerance=±5% power=0.25W resistance=2.2k package=THT]
  R5 = Resistor [tolerance=±5% power=0.25W resistance=2.2k package=THT]
  R6 = Resistor [tolerance=±5% power=0.25W resistance=2.2k package=THT]
  R7 = Resistor [tolerance=±5% power=0.25W resistance=2.2k package=THT]
  R8 = Resistor [tolerance=±5% power=0.25W resistance=2.2k package=THT]
  Bauteil2 = Arduino Mega 2560 (Rev3)
  HC-SR04_Sensor_1 = HC-SR04 Ultrasonic Distance Sensor
  J1 = Piezo Speaker
  7_Segment_4_Digit_Display1 = 7-SEGMENT-4DIGIT common anode [part_number="5461BS - 5462BS" package=7-segment-4digit-anode]

nets:
  N1: R1.Pin_0, Bauteil2.A3
  N2: R1.Pin_1, 7_Segment_4_Digit_Display1.pin_2
  N3: R2.Pin_0, Bauteil2.A7
  N4: R2.Pin_1, 7_Segment_4_Digit_Display1.pin_3
  N5: R3.Pin_0, Bauteil2.A6
  N6: R3.Pin_1, 7_Segment_4_Digit_Display1.pin_5
  N7: R4.Pin_0, Bauteil2.A5
  N8: R4.Pin_1, 7_Segment_4_Digit_Display1.pin_10
  N9: R5.Pin_0, Bauteil2.A4
  N10: R5.Pin_1, 7_Segment_4_Digit_Display1.pin_1
  N11: R6.Pin_0, Bauteil2.A2
  N12: R6.Pin_1, 7_Segment_4_Digit_Display1.pin_4
  N13: R7.Pin_0, Bauteil2.A1
  N14: R7.Pin_1, 7_Segment_4_Digit_Display1.pin_7
  N15: R8.Pin_0, Bauteil2.A0
  N16: R8.Pin_1, 7_Segment_4_Digit_Display1.pin_11
  N17: Bauteil2.A8, 7_Segment_4_Digit_Display1.pin_12
  N18: Bauteil2.A9, 7_Segment_4_Digit_Display1.pin_9
  N19: Bauteil2.A10, 7_Segment_4_Digit_Display1.pin_8
  N20: Bauteil2.A11, 7_Segment_4_Digit_Display1.pin_6
  GND: Bauteil2.GND, HC-SR04_Sensor_1.GND, J1.pin1
  N21: Bauteil2.D12_PWM, J1.pin2
  N22: Bauteil2.D11_PWM, HC-SR04_Sensor_1.TRIG
  N23: Bauteil2.D10_PWM, HC-SR04_Sensor_1.ECHO
  5V: Bauteil2.5V, HC-SR04_Sensor_1.VCC

custom parts:
  7-SEGMENT-4DIGIT common anode: A 7 Segment 4 Digit common anode display, with decimal points

// code stored in the sketch: ultraschall_abstandsmesser_mit_kommentare.ino
#include <TimerFive.h>
#define DIGIT_DELAY   2             // Delay between digits in ms

#define ECHO_PIN      10            // Ultrasound echo pin for pulseIn()
#define IO            PORTB         // Trigger (ultrasound) + beeper
#define IODDR         DDRB

#define PC4MASK       B00010000
#define PB5MASK       B00100000

#define SAMPLES       10            // Number of smaples to be averaged
#define DISPLAYREP    100           // Display n times to minimise flicker

#define ANODEPORT     PORTF         // Control the anodes ot the display
#define ANODEDDR      DDRF          

#define CATHODEPORT   PORTK         // Control the cathodes of the display
#define CATHODEDDR    DDRK

#define BEEPER        B01000000
#define BEEPINTERVAL  400L          // Time on / off
#define THRESHOLD     150           // First threshhold, interval beeping
#define THRESHOLD2    50            // Second threshhold, continous beeping

char numbers[10] = {                // Bit masks for the 7 segement display
    B00111111,                      // digit 0
    B00000110,                      // digit 1
    B01011011,                      // digit 2
    B01001111,                      // digit 3
    B01100110,                      // digit 4
    B01101101,                      // digit 5
    B01111101,                      // digit 6
    B00000111,                      // digit 7
    B01111111,                      // digit 8
    B01101111                       // digit 9
}; 

volatile beep() {                   // Toggle beeper on / off
  IO ^= BEEPER;
}

void showNumber(unsigned int value) {
  unsigned char mask = 0xf7;        // left most digit on
  for(unsigned int i = 0; i < 4; i++)
  {
    CATHODEPORT = mask;             // Activate digit
    ANODEPORT = numbers[value % 10];// Display one decimal digit
    value /= 10;                    // Shift value to the right (decimal)
    delay(DIGIT_DELAY);             // Wait a moment
    mask >>= 1;                     // Prepare to display next digit
  }
  CATHODEPORT = 0xff;               // Switch off the display again
}

void setup() {
  IODDR      = B01100000;           // BP6 = beeper, PB5 = Ultrasound trigger
  CATHODEDDR = B00001111;           // Bit 0..3 control the cathodes
  ANODEDDR   = B11111111;           

  Timer5.attachInterrupt(beep);     // Timer5 controls the interval beeper
  Timer5.initialize(1000L * BEEPINTERVAL);
  Timer5.stop();                    // Make sure nothing beeps at first! :-)
}

void loop() {
  static float duration = 0,        // Return time for ultrasound impulse
    distance;                       // Distance in mm
  static bool timerstate = false;   // Timer5 off or on?

  for (int i = 0; i < SAMPLES; i++) {
    IO |= PB5MASK;                  // Generate an ultrasoud pulse
    delayMicroseconds(2);           // by toggling the IO pin off, on, off
    IO &= ~PB5MASK; 
    delayMicroseconds(10);
    IO |= PB5MASK;

    duration += pulseIn(ECHO_PIN, HIGH);    // How long did it take the
                                            // pulse to return?
  }
  duration /= SAMPLES;                      // Compute the arithmetic mean
  distance = (duration * .0343) / 2 * 10 ;  // Convert to mm

  if (distance <= THRESHOLD && distance > THRESHOLD2 && !timerstate){
    Timer5.start();                 // Turn on annoying beeping
    timerstate = true;              // Remember that it is turned on
  }
  else if (distance > THRESHOLD && timerstate){
    Timer5.stop();                  // Turn off the beeper timer
    IO &= ~BEEPER;                  // and make sure the beeper is off
    timerstate = false;             // and remember this
  } 
  else if (distance <= THRESHOLD2){
    Timer5.stop();                  // We are too cole: Beep continuously
    IO |= BEEPER;
    timerstate = false;
  } 
  else if(distance > THRESHOLD2 && !timerstate){
    Timer5.stop();                  // Stop continuous beeping
    IO &= ~BEEPER;
    timerstate = false;
  }

  for(int i = 0; i < DISPLAYREP; i++)   // Display the distance n times
    showNumber((unsigned int) distance);
}
